# Fritzing sketch genius (saved by Fritzing 0.9.3b)
breadboards: 1

parts:
  Componente1 = Arduino Uno (Rev3)
  R1 = Resistor [tolerance=±5% resistance=220 package=THT]
  R2 = Resistor [tolerance=±5% resistance=220 package=THT]
  R3 = Resistor [tolerance=±5% resistance=220 package=THT]
  R4 = Resistor [tolerance=±5% resistance=220 package=THT]
  LED1 = LED - 3mm [color="Green (555nm)" package="3 mm [THT]"]
  LED2 = LED - 3mm [color="Yellow (585nm)" package="3 mm [THT]"]
  LED3 = LED - 3mm [color="Red (633nm)" package="3 mm [THT]"]
  LED4 = LED - 3mm [color="Blue (430nm)" package="3 mm [THT]"]
  S1 = Pushbutton [package="[THT]"]
  S2 = Pushbutton [package="[THT]"]
  S3 = Pushbutton [package="[THT]"]
  S4 = Pushbutton [package="[THT]"]

nets:
  N1: Componente1.D8, Componente1.D9_PWM, Componente1.D10_PWM/SS, Componente1.D11_PWM/MOSI, Componente1.GND, R1.Pin_0, R2.Pin_0, R3.Pin_0, R4.Pin_0, S1.Pin_3, S1.Pin_4, S2.Pin_3, S2.Pin_4, S3.Pin_3, S3.Pin_4, S4.Pin_3, S4.Pin_4
  N2: Componente1.D2, LED1.anode
  N3: Componente1.D3_PWM, LED2.anode
  N4: Componente1.D4, LED3.anode
  N5: Componente1.D5_PWM, LED4.anode
  N6: R1.Pin_1, LED2.cathode
  N7: R2.Pin_1, LED3.cathode
  N8: R3.Pin_1, LED4.cathode
  N9: R4.Pin_1, LED1.cathode
  N10: S1.Pin_1, S1.Pin_2
  N11: S2.Pin_1, S2.Pin_2
  N12: S3.Pin_1, S3.Pin_2
  N13: S4.Pin_1, S4.Pin_2
