# Fritzing sketch input_pullup (saved by Fritzing 0.9.3b)
breadboards: 1

parts:
  Componente1 = Arduino Uno (Rev3)
  S1 = Pushbutton [package="[THT]"]

nets:
  N1: Componente1.D13/SCK, Componente1.GND, S1.Pin_3, S1.Pin_4
  N2: S1.Pin_1, S1.Pin_2

notes:
  Ao usar a função pullup e o botão ligado no ground, o botão irá "roubar" a energia do circuito, deixando-o no estado LOW (0).
  Por isso não devemos energizar o circuito.
