# Fritzing sketch leds (saved by Fritzing 0.9.3b)
breadboards: 1

parts:
  Componente1 = Arduino Uno (Rev3)
  R1 = Resistor [tolerance=±5% resistance=220 package=THT]
  R2 = Resistor [tolerance=±5% resistance=220 package=THT]
  R3 = Resistor [tolerance=±5% resistance=220 package=THT]
  R4 = Resistor [tolerance=±5% resistance=220 package=THT]
  LED2 = LED - 3mm [color="Blue (430nm)" package="3 mm [THT]"]
  LED3 = LED - 3mm [color="Red (633nm)" package="3 mm [THT]"]
  LED4 = LED - 3mm [color="Yellow (585nm)" package="3 mm [THT]"]
  LED5 = LED - 3mm [color="Green (555nm)" package="3 mm [THT]"]

nets:
  N1: Componente1.D2, LED5.anode
  N2: Componente1.D3_PWM, LED4.anode
  N3: Componente1.D4, LED3.anode
  N4: Componente1.D5_PWM, LED2.anode
  N5: Componente1.GND, R1.Pin_1, R2.Pin_0, R3.Pin_0, R4.Pin_0
  N6: R1.Pin_0, LED2.cathode
  N7: R2.Pin_1, LED3.cathode
  N8: R3.Pin_1, LED5.cathode
  N9: R4.Pin_1, LED4.cathode
